# Fritzing sketch Main (saved by Fritzing 0.9.4)

parts:
  M1 = RioRand LM2596
  Componente1 = Arduino Mega 2560 (Rev3)
  J1 = Basic Servo  # not connected

nets:
  N1: M1.Pin_3, Componente1.VIN
  N2: M1.Pin_4, Componente1.GND
